// Logisim project 1 - 1 bit full adder.circ as structural Verilog: 1 circuit, main circuit main
module main (
  input  in_1,
  input  in_2,
  input  in_3,
  output out_4,
  output out_5
);

  Adder #(.width(1)) adder_1 (.a(in_2), .b(in_3), .out(out_4), .cin(in_1), .cout(out_5));
  LED led_1 (.in(out_5));
  LED led_2 (.in(out_4));
endmodule
