// Logisim project 2 - 4 bit binary adder subtractor.circ as structural Verilog: 1 circuit, main circuit main
module main (
  input  in_1,
  input  in_2,
  input  in_3,
  input  in_4,
  input  in_5,
  input  in_6,
  input  in_7,
  input  in_8,
  input  in_9,
  output S0,
  output S1,
  output S2,
  output S3,
  output V,
  output C
);

  wire adder_1_cout, adder_2_cout, adder_3_cout, xor_1_out, xor_2_out, xor_3_out, xor_4_out;

  xor xor_1 (xor_1_out, in_3, in_1);
  xor xor_2 (xor_2_out, in_5, in_1);
  xor xor_3 (xor_3_out, in_7, in_1);
  xor xor_4 (xor_4_out, in_9, in_1);
  Adder #(.width(1)) adder_1 (.a(in_2), .b(xor_1_out), .out(S0), .cin(in_1), .cout(adder_1_cout));
  Adder #(.width(1)) adder_2 (.a(in_4), .b(xor_2_out), .out(S1), .cin(adder_1_cout), .cout(adder_2_cout));
  Adder #(.width(1)) adder_3 (.a(in_6), .b(xor_3_out), .out(S2), .cin(adder_2_cout), .cout(adder_3_cout));
  Adder #(.width(1)) adder_4 (.a(in_8), .b(xor_4_out), .out(S3), .cin(adder_3_cout), .cout(C));
  xor xor_5 (V, adder_3_cout, C);
endmodule
